# Fritzing sketch 2-factor-door-lock (saved by Fritzing 0.9.3b)

parts:
  Part1 = Arduino Uno (Rev3) - ICSP
  LCD3 = LCD screen
  LCM1602_IIC3 = LCM1602 IIC [part_number="LCM1602 IIC" chip_label="LCM1602 IIC" package="DIP (Dual Inline) [THT]"]
  KEYPAD1 = Membrane Matrix Keypad

nets:
  N1: Part1.D8, KEYPAD1.3
  N2: Part1.D9_PWM, KEYPAD1.2
  N3: Part1.D10_PWM/SS, KEYPAD1.1
  N4: Part1.A4/SDA, LCM1602_IIC3.SDA
  N5: Part1.A5/SCL, LCM1602_IIC3.SCL
  N6: Part1.D4, KEYPAD1.7
  N7: Part1.D5_PWM, KEYPAD1.6
  N8: Part1.D6_PWM, KEYPAD1.5
  N9: Part1.D7, KEYPAD1.4
  5V: Part1.5V, LCM1602_IIC3.VCC
  GND: Part1.GND, LCM1602_IIC3.GND
  VSS: LCD3.VSS, LCM1602_IIC3.VSS
  VDD: LCD3.VDD, LCM1602_IIC3.VDD
  N10: LCD3.V0, LCM1602_IIC3.V0
  N11: LCD3.RS, LCM1602_IIC3.RS
  N12: LCD3.R/W, LCM1602_IIC3.RW
  N13: LCD3.E, LCM1602_IIC3.E
  N14: LCD3.DB0, LCM1602_IIC3.D0
  N15: LCD3.DB1, LCM1602_IIC3.D1
  N16: LCD3.DB2, LCM1602_IIC3.D2
  N17: LCD3.DB3, LCM1602_IIC3.D3
  N18: LCD3.DB4, LCM1602_IIC3.D4
  N19: LCD3.DB5, LCM1602_IIC3.D5
  N20: LCD3.DB6, LCM1602_IIC3.D6
  N21: LCD3.DB7, LCM1602_IIC3.D7
  N22: LCD3.LED+, LCM1602_IIC3.A
  N23: LCD3.LED-, LCM1602_IIC3.K

notes:
  RX of R307
  TX of R307
  Vcc of R307
  GND of R307

custom parts:
  LCM1602 IIC: I2C-Module to use a 1602 or 2004 LCD on with the wire.h libory Serial LCD Modul
  Membrane Matrix Keypad: Membrane Matrix 3x4 Keypad
